// Logisim project and or add sub.circ as structural Verilog: 1 circuit, main circuit main
module main (
  input  A0,
  input  B0,
  input  A0_2,
  input  B0_2,
  input  A0_3,
  input  B0_3,
  input  A0_4,
  input  B0_4,
  input  [1:0] in_9,
  input  minus_B,
  output R0,
  output R0_2,
  output R0_3,
  output R0_4
);

  wire adder_1_cout, adder_1_out, adder_2_out, adder_3_out, adder_4_cout, adder_4_out, and_1_out, and_2_out,
       and_3_out, and_4_out, multiplexer_1_out, multiplexer_2_out, multiplexer_3_out, multiplexer_4_out,
       not_1_out, not_2_out, not_3_out, not_4_out, or_1_out, or_2_out, or_3_out, or_4_out;

  Multiplexer multiplexer_1 (.in0(B0), .in1(not_1_out), .out(multiplexer_1_out), .sel(minus_B));  // open: en
  not not_1 (not_1_out, B0);
  Multiplexer multiplexer_2 (.in0(B0_2), .in1(not_2_out), .out(multiplexer_2_out), .sel(minus_B));  // open: en
  not not_2 (not_2_out, B0_2);
  Multiplexer multiplexer_3 (.in0(B0_3), .in1(not_3_out), .out(multiplexer_3_out), .sel(minus_B));  // open: en
  not not_3 (not_3_out, B0_3);
  Multiplexer multiplexer_4 (.in0(B0_4), .in1(not_4_out), .out(multiplexer_4_out), .sel(minus_B));  // open: en
  not not_4 (not_4_out, B0_4);
  and and_1 (and_1_out, A0, multiplexer_1_out);
  or or_1 (or_1_out, A0, multiplexer_1_out);
  Adder #(.width(1)) adder_1 (.a(A0), .b(multiplexer_1_out), .out(adder_1_out), .cin(minus_B), .cout(adder_1_cout));
  and and_2 (and_2_out, A0_2, multiplexer_2_out);
  or or_2 (or_2_out, A0_2, multiplexer_2_out);
  Adder #(.width(1)) adder_2 (.a(A0_2), .b(multiplexer_2_out), .out(adder_2_out), .cin(adder_1_cout), .cout(minus_B));
  and and_3 (and_3_out, A0_3, multiplexer_3_out);
  or or_3 (or_3_out, A0_3, multiplexer_3_out);
  Adder #(.width(1)) adder_3 (.a(A0_3), .b(multiplexer_3_out), .out(adder_3_out), .cin(minus_B), .cout(minus_B));
  and and_4 (and_4_out, A0_4, multiplexer_4_out);
  or or_4 (or_4_out, A0_4, multiplexer_4_out);
  Adder #(.width(1)) adder_4 (.a(A0_4), .b(multiplexer_4_out), .out(adder_4_out), .cin(minus_B), .cout(adder_4_cout));
  Multiplexer #(.select(2)) multiplexer_5 (
    .in0(and_1_out), .in1(or_1_out), .in2(adder_1_out), .out(R0), .sel(in_9));  // open: in3, en
  Multiplexer #(.select(2)) multiplexer_6 (
    .in0(and_2_out), .in1(or_2_out), .in2(adder_2_out), .out(R0_2), .sel(in_9));  // open: in3, en
  Multiplexer #(.select(2)) multiplexer_7 (
    .in0(and_3_out), .in1(or_3_out), .in2(adder_3_out), .out(R0_3), .sel(in_9));  // open: in3, en
  Multiplexer #(.select(2)) multiplexer_8 (
    .in0(and_4_out), .in1(or_4_out), .in2(adder_4_out), .out(R0_4), .sel(in_9));  // open: in3, en
endmodule
